# Fritzing sketch Smart Motor Overload Protection System (saved by Fritzing 0.9.3b)
breadboards: 1

parts:
  U1 = NodeMCU V1.0
  L298N1 = L298N DC motor driver
  VCC1 = Battery
  M1 = Getriebemotor
  KY-1 = Keyes Relay [package=THT]
  Q1 = NPN-Transistor [package="TO92 [THT]"]
  R1 = Resistor [tolerance=±5% resistance=1k package="2512 [SMD]"]
  R2 = Resistor [tolerance=±5% resistance=1k package="2512 [SMD]"]
  Part1 = ACS712 Current Sensor 5A 20A 30A
  R3 = Resistor [tolerance=±5% resistance=100 package="2512 [SMD]"]
  R4 = Resistor [tolerance=±5% resistance=100 package="2512 [SMD]"]
  R5 = Resistor [tolerance=±5% resistance=100 package="2512 [SMD]"]

nets:
  GND: U1.GND, Q1.E, Part1.GND, R5.Pin_1
  N1: U1.D5, R2.Pin_1
  N2: U1.D6, L298N1.IN1
  N3: U1.D7, L298N1.IN2
  VIN: U1.Vin, KY-1.power, R1.Pin_1, Part1.VCC
  N4: U1.A0, R3.Pin_1, R4.Pin_0
  N5: L298N1.OUT1, Part1.1
  N6: L298N1.OUT2, M1.pin_1
  N7: L298N1.12V, KY-1.NC
  N8: L298N1.GND, VCC1.-
  N9: L298N1.5V, L298N1.ENA
  N10: VCC1.+, KY-1.C
  N11: M1.pin_2, Part1.2, Part1.OUT, R3.Pin_0
  N12: KY-1.signal, R1.Pin_0
  N13: KY-1.ground, Q1.C
  N14: Q1.B, R2.Pin_0
  N15: R4.Pin_1, R5.Pin_0

custom parts:
  NodeMCU V1.0: ESP8266 based NodeMCU
  L298N DC motor driver: 2x DC motor driver with 78M05 positive voltage regulator (7..35 V) L298N: max 46 V, 2 A Set 5 V Enable jumper to enable 5 V regultor (needed for the L298N) and +5 V output at screw terminal or supply external +5 V at screw terminal Set ENA and/or ENB to +5 V to enable motor permanently or supply ENA and/or ENB with PWM signal IN1 and IN2 set rotation directory for motor A (OUT1/OUT2) IN2 and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
  Battery: Your standard 3x 18650 battery pack (11.1 Volts)
  Keyes Relay: The Keyes 5V relay module is suitable for SCM development, home appliance control. It uses a 5V~12V TIL control signal which can control DC / AC signal.
  ACS712 Current Sensor 5A 20A 30A: Remix by Michael Kubina http://www.kubina.info Original by: https://forum.fritzing.org/t/current-sensor-5a-acs712/7694 https://forum.fritzing.org/u/ArtHome ArtHome12@gmail.com
